// Logisim project microcode-fsm.circ as structural Verilog: 2 circuits, main circuit main
module main (
);

  wire branch, clk;
  wire [1:0] branch_logic_1_mux;
  wire [4:0] adder_1_out, addr, multiplexer_1_out, register_1_q;
  wire [7:0] register_2_q;
  wire [7:5] instr;

  Adder #(.width(5)) adder_1 (.a(5'b00001), .b(register_1_q), .out(adder_1_out), .cin(1'b0));  // open: cout
  branch_logic branch_logic_1 (.op_mux(instr[6:5]), .branch(branch), .mux(branch_logic_1_mux));
  Clock clock_1 (.out(clk));
  Multiplexer #(.select(2), .width(5)) multiplexer_1 (
    .in0(adder_1_out), .in1(addr), .in2({5{1'b0}}), .out(multiplexer_1_out), .sel(branch_logic_1_mux),
    .en(1'b1));  // open: in3
  Register #(.width(5)) register_1 (.D(multiplexer_1_out), .en(1'b1), .Q(register_1_q), .clk(clk));  // open: clr
  Register register_2 (.D({instr, addr}), .en(branch), .Q(register_2_q), .clk(clk));  // open: clr
  _7_Segment_Display u_7_segment_display_1 (
    .g(register_2_q[0]), .f(register_2_q[1]), .a(register_2_q[2]), .b(register_2_q[3]), .e(register_2_q[4]),
    .d(register_2_q[5]), .c(register_2_q[6]), .dp(register_2_q[7]));
  ROM #(.addrWidth(5), .dataWidth(9)) rom_1 (.addr(register_1_q), .data({branch, instr, addr}), .sel(1'b1));

  // Other names for the same wires on the sheet: instr (some bits) = {branch, addr}; out[7:0] = {instr, addr};
  //   mux[1:0] = instr[6:5]

  // Notes on the sheet:
  //   Branch
  //   Branch logic
  //   uPC
  //   Output
  //   Output
  //   contents of rom_1 (hex, n*v repeats v):
  //   100 148 13d 16d 14b 167 177 14c 17f 16f 20
endmodule

module branch_logic (
  input  [1:0] op_mux,
  input  branch,
  output [1:0] mux
);

  wire not_1_out;

  not not_1 (not_1_out, branch);
  and and_1 (mux[0], not_1_out, op_mux[0]);
  and and_2 (mux[1], op_mux[1], not_1_out);
endmodule
